# Fritzing sketch ESP8266-DHT11-LCD1602_I2C-SG90-RC522 (saved by Fritzing 0.9.3b)
breadboards: 1

parts:
  U1 = NodeMCU V3.0
  元件1 = LCD1602-I2C
  DHT1 = DHT11 Humitidy and Temperature Sensor (3 pins)
  SERVO1 = Tower Pro SG90 servo [part_number=101246]
  元件2 = RFID-RC522-v3

nets:
  N1: U1.D0, SERVO1.Signal
  N2: U1.D1, 元件1.SCL
  N3: U1.D2, 元件1.SDA
  N4: U1.D3, 元件2.RST
  3V3: U1.3V3, DHT1.DATA, SERVO1.+5V, 元件2.3.3V
  GND: U1.GND#6, U1.GND#13, U1.GND#33, DHT1.GND, SERVO1.GND, 元件2.GND
  N5: U1.D5, 元件2.SCK
  N6: U1.D6, 元件2.MISO
  N7: U1.D7, 元件2.MOSI
  N8: U1.D8, 元件2.SDA
  N9: U1.RX, DHT1.VDD
  VIN: U1.Vin, 元件1.VCC
  N10: U1.GND#41, 元件1.GND

custom parts:
  NodeMCU V3.0: ESP8266 based NodeMCU
  LCD1602-I2C: A standard character display, usually with 2x16 characters. Comes in many colors with LCM1602 IIC attached.
  DHT11 Humitidy and Temperature Sensor (3 pins): DHT11 Humidity and Temperature Sensor (3 pins) from the design created by John De Cristofaro for Adafruit Industries.
  Tower Pro SG90 servo: Original file by John De Cristofaro http://www.adafruit.com/products/1449 Adafruit Feedback Servo (Small) Edited by: e-radionica.com 28/9/2015
  RFID-RC522-v3: A simple China made RFID-RC522 Reader (6x4 cm); do check the pin labels, as this is a MFRC522 based clone.
